# Fritzing sketch coaster (saved by Fritzing 1.0.4)

parts:
  Trill_Craft1 = Trill Craft
  Part1 = Adafruit DRV2605L [part_number="Adafruit #2305"]
  A1 = seeeduino-xiao

nets:
  N1: Trill_Craft1.SCL, Part1.SCL, A1.D5
  N2: Trill_Craft1.SDA, Part1.SDA, A1.D4
  VCC: Trill_Craft1.VCC, Part1.VIN, A1.5V
  GND: Trill_Craft1.GND, Part1.GND, A1.GND

custom parts:
  Trill Craft: A 30-channel breakout board for building touch interfaces out of any conductive material, by Bela.io
  Adafruit DRV2605L: The DRV2605 from TI is a fancy little motor driver. Rather than controlling a stepper motor or DC motor, its designed specifically for controlling haptic motors - buzzers and vibration motors. Normally one would just turn those kinds of motors on and off, but this driver has the ability to have various effects when driving a vibe motor. For example, ramping the vibration level up and down,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
  seeeduino-xiao: Seeeduino XIAO processor board SMD version.
