# Fritzing sketch curtain (saved by Fritzing 1.0.4)

parts:
  M1 = Arduino NANO RP2040 CONNECT with headers
  R1 = Rotary Potentiometer (Small) [maximum_resistance=100kΩ knob_status=50% power=0.5W package=THT]
  Mod1 = KY-002 Vibration Switch Module [package="Breakout board"]

nets:
  N1: M1.GND-4, M1.GND-29, R1.leg1, Mod1.-
  N2: M1.D13, R1.leg2, Mod1.S
  N3: M1.D14, R1.wiper
  N4: M1.D19, Mod1.Vin

custom parts:
  KY-002 Vibration Switch Module: Arduino Vibration Switch Module KY-002 Keyes allows detection of shock and vibration.
