# Fritzing sketch pillow (saved by Fritzing 1.0.4)

parts:
  Mod1 = Amica NodeMCU DEVKIT 1.0
  R1 = Temperature Sensor (Thermistor) [thermistor_type=NTC package=THT]
  Part1 = Adafruit DRV2605L [part_number="Adafruit #2305"]
  Part2 = Adafruit BMP180
  R2 = Resistor [tolerance=±5% resistance=220 package="2010 [SMD]"]

nets:
  GND: Mod1.pin2, Mod1.pin_9, Mod1.pin_25, Mod1.pin_29, R1.pin_0, Part1.GND, Part2.GND
  N1: Mod1.pin_10, Mod1.pin_26, R2.Pin_1
  N2: Mod1.pin_13, Part1.SDA, Part2.SDA
  N3: Mod1.pin_14, Part1.SCL, Part2.SCL
  N4: Mod1.pin_16, R2.Pin_0
  VIN: Mod1.pin_30, Part1.VIN, Part2.+5V

notes:
  The schematic uses a thermistor in place of conductive rubber band
  Capacitive touch pin

custom parts:
  Adafruit DRV2605L: The DRV2605 from TI is a fancy little motor driver. Rather than controlling a stepper motor or DC motor, its designed specifically for controlling haptic motors - buzzers and vibration motors. Normally one would just turn those kinds of motors on and off, but this driver has the ability to have various effects when driving a vibe motor. For example, ramping the vibration level up and down,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
  Adafruit BMP180: This precision sensor from Bosch is the best low-cost sensing solution for measuring barometric pressure and temperature. Because pressure changes with altitude you can also use it as an altimeter! The sensor is soldered onto a PCB with a 3.3V regulator, I2C level shifter and pull-up resistors on the I2C pins. The BMP180 is the next-generation of sensors from Bosch, and replaces the BMP085.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
